// Logisim project Architecture.circ as structural Verilog
module main (
  input  in_1,
  input  in_2,
  input  in_3,
  output out_4
);

  wire my_not_1_out_2, my_or_1_out_3;

  my_or my_or_1 (.in_1(in_1), .in_2(in_2), .out_3(my_or_1_out_3));
  my_not my_not_1 (.a(in_3), .out_2(my_not_1_out_2));
  my_and my_and_1 (.x(my_or_1_out_3), .y(my_not_1_out_2), .out_3(out_4));
endmodule

module my_not (
  input  a,
  output out_2
);

  nand nand_1 (out_2, a, a);
endmodule

module my_and (
  input  x,
  input  y,
  output out_3
);

  wire nand_1_out;

  nand nand_1 (nand_1_out, x, y);
  my_not my_not_1 (.a(nand_1_out), .out_2(out_3));
endmodule

module my_or (
  input  in_1,
  input  in_2,
  output out_3
);

  wire my_and_1_out_3, my_not_1_out_2, my_not_2_out_2;

  my_not my_not_1 (.a(in_1), .out_2(my_not_1_out_2));
  my_not my_not_2 (.a(in_2), .out_2(my_not_2_out_2));
  my_and my_and_1 (.x(my_not_1_out_2), .y(my_not_2_out_2), .out_3(my_and_1_out_3));
  my_not my_not_3 (.a(my_and_1_out_3), .out_2(out_3));
endmodule

module my_Xor (
  input  in_1,
  input  in_2,
  output out_3
);

  wire my_and_1_out_3, my_and_2_out_3, my_not_1_out_2, my_not_2_out_2;

  my_not my_not_1 (.a(in_2), .out_2(my_not_1_out_2));
  my_not my_not_2 (.a(in_1), .out_2(my_not_2_out_2));
  my_and my_and_1 (.x(in_1), .y(my_not_1_out_2), .out_3(my_and_1_out_3));
  my_and my_and_2 (.x(my_not_2_out_2), .y(in_2), .out_3(my_and_2_out_3));
  my_or my_or_1 (.in_1(my_and_1_out_3), .in_2(my_and_2_out_3), .out_3(out_3));
endmodule

module my_MUX (
  input  a,
  input  sel,
  input  b,
  output out_4
);

  wire my_and_1_out_3, my_and_2_out_3, my_not_1_out_2;

  my_not my_not_1 (.a(sel), .out_2(my_not_1_out_2));
  my_and my_and_1 (.x(a), .y(sel), .out_3(my_and_1_out_3));
  my_and my_and_2 (.x(my_not_1_out_2), .y(b), .out_3(my_and_2_out_3));
  my_or my_or_1 (.in_1(my_and_1_out_3), .in_2(my_and_2_out_3), .out_3(out_4));
endmodule

module my_DMux (
  input  i_n,
  input  sel,
  output out_3,
  output out_4
);

  wire my_not_1_out_2;

  my_not my_not_1 (.a(sel), .out_2(my_not_1_out_2));
  my_and my_and_1 (.x(i_n), .y(sel), .out_3(out_3));
  my_and my_and_2 (.x(i_n), .y(my_not_1_out_2), .out_3(out_4));
endmodule

module my_Not4 (
  input  [3:0] in_1,
  output [3:0] out_2
);

  my_not my_not_1 (.a(in_1[0]), .out_2(out_2[0]));
  my_not my_not_2 (.a(in_1[1]), .out_2(out_2[1]));
  my_not my_not_3 (.a(in_1[2]), .out_2(out_2[2]));
  my_not my_not_4 (.a(in_1[3]), .out_2(out_2[3]));
endmodule

module my_And4 (
  input  [3:0] in_1,
  input  [3:0] in_2,
  output [3:0] out_3
);

  my_and my_and_1 (.x(in_1[0]), .y(in_2[0]), .out_3(out_3[0]));
  my_and my_and_2 (.x(in_1[1]), .y(in_2[1]), .out_3(out_3[1]));
  my_and my_and_3 (.x(in_1[2]), .y(in_2[2]), .out_3(out_3[2]));
  my_and my_and_4 (.x(in_1[3]), .y(in_2[3]), .out_3(out_3[3]));
endmodule
